# Fritzing sketch rfm95w_adapter (saved by Fritzing 0.9.3b)
circuit board: 2.54cm x 1.38674cm

parts:
  J3 = female alternating pin header, 5 pins [form="♀ (female)"]  # not connected
  J2 = female alternating pin header, 5 pins [form="♀ (female)"]
  J1 = female alternating pin header, 3 pins [form="♀ (female)"]
  J4 = female alternating pin header, 5 pins [form="♀ (female)"]

nets:
  N1: J2.pin2, J1.pin1
  N2: J2.pin3, J4.pin1
  N3: J2.pin4, J1.pin3
  N4: J2.pin5, J1.pin2

notes:
  tmb.gr/iot
  FeatherWing RFM95W LoRaWAN Adapter
  For pinout and software configuration, see
  https://github.com/tamberg/fhnw-iot/wiki/FeatherWing-RFM95W
  Check the PCB view to see the design.
  CC BY-SA 4.0 Thomas Amberg, FHNW.
  Thanks to Radomir Dopieralski, SGMK.
  FeatherWing RFM95W LoRaWAN Adapter
  For pinout and software configuration, see
  https://github.com/tamberg/fhnw-iot/wiki/FeatherWing-RFM95W
  CC BY-SA 4.0 Thomas Amberg, FHNW.
  Thanks to Radomir Dopieralski, SGMK.
  v2
